# Fritzing sketch Lunchbox_Fritzing_Diagram (saved by Fritzing 0.7.12b)
stripboards: 1

parts:
  Part1 = Arduino Pro Mini 3.3V
  T1 = LM35 Temperature Sensor [package="TO92 [THT]"]
  VCC1 = Battery block 9V
  J1 = male pin header, 6 pins [form="♂ (male)"]

nets:
  N1: Part1.RAW, VCC1.+
  GND: Part1.GND, T1.GND, VCC1.-, J1.pin2
  N2: Part1.VCC, T1.+Vs, J1.pin1
  N3: Part1.A0, T1.Vout
  N4: Part1.SCK, J1.pin5
  N5: Part1.MOSI, J1.pin3
  N6: Part1.D10, J1.pin4
